# Fritzing sketch eksamen (saved by Fritzing 0.9.8b)
breadboards: 1

parts:
  Part1 = Adafruit Mini TFT Display - 0.96in 160x80 [part_number="Adafruit 3533"]
  Part2 = Arduino Uno (Rev3) - ICSP
  S1 = Pushbutton [package="[THT]"]
  S2 = Pushbutton [package="[THT]"]
  S3 = Pushbutton [package="[THT]"]
  S4 = Pushbutton [package="[THT]"]
  J1 = Piezo Speaker
  Part3 = Thumb Joystick
  R1 = Resistor [tolerance=±5% resistance=10k package="0603 [SMD]"]
  R2 = Resistor [tolerance=±5% resistance=10k package="0603 [SMD]"]
  R3 = Resistor [tolerance=±5% resistance=10k package="0603 [SMD]"]
  R4 = Resistor [tolerance=±5% resistance=10k package="0603 [SMD]"]
  R5 = Resistor [tolerance=±5% resistance=220 package="0603 [SMD]"]

nets:
  3.3V: Part1.3.3V, Part2.5V, S1.Pin_1, S1.Pin_2, S2.Pin_1, S2.Pin_2, S3.Pin_1, S3.Pin_2, S4.Pin_1, S4.Pin_2, Part3.VCC
  GND: Part1.GND, Part2.A2, Part2.GND, Part3.GND, Part3.SEL, R2.Pin_0, R3.Pin_0, R4.Pin_0, R5.Pin_0
  N1: Part1.SCK, Part2.D13/SCK
  N2: Part1.MOSI, Part2.D11_PWM/MOSI
  N3: Part1.TFTCS, Part2.D10_PWM/SS
  N4: Part1.DC, Part2.D8
  N5: Part2.A0, Part3.HORZ
  N6: Part2.A1, Part3.VERT
  N7: Part2.D2, S2.Pin_3, S2.Pin_4, R4.Pin_1
  N8: Part2.D3_PWM, S3.Pin_3, S3.Pin_4, R1.Pin_0
  N9: Part2.D4, S4.Pin_3, S4.Pin_4, R2.Pin_1
  N10: Part2.D5_PWM, S1.Pin_3, S1.Pin_4, R3.Pin_1
  N11: Part2.D7, J1.pin2
  N12: J1.pin1, R5.Pin_1

custom parts:
  Adafruit Mini TFT Display - 0.96in 160x80: It's the size of your thumbnail, with glorious 160x80 pixel color... it's the Adafruit Mini TFT Breakout! This very very small display is only 0.96" diagonal, packed with RGB pixels, for making very small high-density displays. The display uses 4-wire SPI to communicate and has its own pixel-addressable frame buffer, it can be used with every kind of microcontroller. Even a very small one with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
